// Logisim project Game.circ as structural Verilog: 4 circuits, main circuit main
module main (
  input  in_1,
  output [1:0] Strike,
  output [1:0] Ball
);

  wire button_1_out, button_2_out, button_3_out, button_4_out, button_5_out, button_6_out, dipswitch_1_sw1,
       dipswitch_2_sw1, dipswitch_3_sw1, dipswitch_4_sw1, dipswitch_5_sw1, dipswitch_6_sw1;
  wire [1:0] ballcounter_1_out_7, bit3cpr_1_out_7;
  wire [3:0] udcounter_1_out_7, udcounter_1_out_8, udcounter_1_out_9, udcounter_2_out_7, udcounter_2_out_8,
       udcounter_2_out_9;

  UDCounter udcounter_1 (
    .UPDOWN(dipswitch_1_sw1), .CLK(button_1_out), .in_3(dipswitch_2_sw1), .in_4(button_2_out),
    .in_5(dipswitch_3_sw1), .in_6(button_3_out), .out_7(udcounter_1_out_7), .out_8(udcounter_1_out_8),
    .out_9(udcounter_1_out_9));
  Button button_1 (.out(button_1_out));
  DipSwitch #(.number(2)) dipswitch_1 (.sw1(dipswitch_1_sw1));  // open: sw2
  DipSwitch #(.number(2)) dipswitch_2 (.sw1(dipswitch_2_sw1));  // open: sw2
  Button button_2 (.out(button_2_out));
  Button button_3 (.out(button_3_out));
  DipSwitch #(.number(2)) dipswitch_3 (.sw1(dipswitch_3_sw1));  // open: sw2
  Hex_Digit_Display hex_digit_display_1 (.value(udcounter_1_out_7));  // open: dp
  Hex_Digit_Display hex_digit_display_2 (.value(udcounter_1_out_8));  // open: dp
  Hex_Digit_Display hex_digit_display_3 (.value(udcounter_1_out_9));  // open: dp
  assign Strike = in_1 ? bit3cpr_1_out_7 : 2'bz;  // Controlled_Buffer controlled_buffer_1
  bit3cpr bit3cpr_1 (
    .a1(udcounter_2_out_9), .a2(udcounter_2_out_8), .a3(udcounter_2_out_7), .b1(udcounter_1_out_9),
    .b2(udcounter_1_out_8), .b3(udcounter_1_out_7), .out_7(bit3cpr_1_out_7));
  assign Ball = in_1 ? ballcounter_1_out_7 : 2'bz;  // Controlled_Buffer controlled_buffer_2
  ballcounter ballcounter_1 (
    .a1(udcounter_2_out_9), .a2(udcounter_2_out_8), .a3(udcounter_2_out_7), .b1(udcounter_1_out_9),
    .b2(udcounter_1_out_8), .b3(udcounter_1_out_7), .out_7(ballcounter_1_out_7));
  UDCounter udcounter_2 (
    .UPDOWN(dipswitch_4_sw1), .CLK(button_4_out), .in_3(dipswitch_5_sw1), .in_4(button_5_out),
    .in_5(dipswitch_6_sw1), .in_6(button_6_out), .out_7(udcounter_2_out_7), .out_8(udcounter_2_out_8),
    .out_9(udcounter_2_out_9));
  DipSwitch #(.number(2)) dipswitch_4 (.sw1(dipswitch_4_sw1));  // open: sw2
  Button button_4 (.out(button_4_out));
  Button button_5 (.out(button_5_out));
  DipSwitch #(.number(2)) dipswitch_5 (.sw1(dipswitch_5_sw1));  // open: sw2
  DipSwitch #(.number(2)) dipswitch_6 (.sw1(dipswitch_6_sw1));  // open: sw2
  Button button_6 (.out(button_6_out));
  Hex_Digit_Display hex_digit_display_4 (.value(udcounter_2_out_7));  // open: dp
  Hex_Digit_Display hex_digit_display_5 (.value(udcounter_2_out_8));  // open: dp
  Hex_Digit_Display hex_digit_display_6 (.value(udcounter_2_out_9));  // open: dp

  // Notes on the sheet:
  //   Trying Part
  //   1번 스위치 : UP일 경우 숫자 증가, Down일 경우 숫자 감소
  //   정답 제출 시 1로, 숫자 변경할때는 1
  //   숫자아구
  //   Setting Part
  //   1번 스위치 : UP일 경우 숫자 증가, Down일 경우 숫자 감소
endmodule

module UDCounter (
  input  UPDOWN,
  input  CLK,
  input  in_3,
  input  in_4,
  input  in_5,
  input  in_6,
  output [3:0] out_7,
  output [3:0] out_8,
  output [3:0] out_9
);

  wire and_1_out, and_2_out, and_3_out, and_4_out, and_5_out, and_6_out, and_7_out, and_8_out, and_9_out,
       and_10_out, and_11_out, and_12_out, and_13_out, and_14_out, and_15_out, and_16_out, and_17_out,
       and_18_out, j_k_ff_1_qn, j_k_ff_2_qn, j_k_ff_3_qn, j_k_ff_4_qn, j_k_ff_5_qn, j_k_ff_6_qn, j_k_ff_7_qn,
       j_k_ff_8_qn, j_k_ff_9_qn, not_1_out, not_2_out, not_3_out, or_1_out, or_2_out, or_3_out, or_4_out,
       or_5_out, or_6_out, or_7_out, or_8_out, or_9_out;

  J_K_Flip_Flop j_k_ff_1 (.J(1'b1), .K(1'b1), .clk(in_6), .Q(out_9[0]), .Qn(j_k_ff_1_qn));  // open: preset, reset
  J_K_Flip_Flop j_k_ff_2 (.J(1'b1), .K(1'b1), .clk(CLK), .Q(out_7[0]), .Qn(j_k_ff_2_qn));  // open: preset, reset
  not not_1 (not_1_out, UPDOWN);
  J_K_Flip_Flop j_k_ff_3 (.J(1'b1), .K(1'b1), .clk(in_4), .Q(out_8[0]), .Qn(j_k_ff_3_qn));  // open: preset, reset
  not not_2 (not_2_out, in_3);
  not not_3 (not_3_out, in_5);
  and and_1 (and_1_out, UPDOWN, out_7[0]);
  and and_2 (and_2_out, j_k_ff_2_qn, not_1_out);
  and and_3 (and_3_out, in_3, out_8[0]);
  and and_4 (and_4_out, j_k_ff_3_qn, not_2_out);
  and and_5 (and_5_out, in_5, out_9[0]);
  and and_6 (and_6_out, j_k_ff_1_qn, not_3_out);
  or or_1 (or_1_out, and_1_out, and_2_out);
  or or_2 (or_2_out, and_3_out, and_4_out);
  or or_3 (or_3_out, and_5_out, and_6_out);
  J_K_Flip_Flop j_k_ff_4 (
    .J(or_1_out), .K(or_1_out), .clk(CLK), .Q(out_7[1]), .Qn(j_k_ff_4_qn));  // open: preset, reset
  J_K_Flip_Flop j_k_ff_5 (
    .J(or_2_out), .K(or_2_out), .clk(in_4), .Q(out_8[1]), .Qn(j_k_ff_5_qn));  // open: preset, reset
  J_K_Flip_Flop j_k_ff_6 (
    .J(or_3_out), .K(or_3_out), .clk(in_6), .Q(out_9[1]), .Qn(j_k_ff_6_qn));  // open: preset, reset
  and and_7 (and_7_out, and_1_out, out_7[1]);
  and and_8 (and_8_out, j_k_ff_4_qn, and_2_out);
  and and_9 (and_9_out, and_3_out, out_8[1]);
  and and_10 (and_10_out, j_k_ff_5_qn, and_4_out);
  and and_11 (and_11_out, and_5_out, out_9[1]);
  or or_4 (or_4_out, and_11_out, and_12_out);
  and and_12 (and_12_out, j_k_ff_6_qn, and_6_out);
  J_K_Flip_Flop j_k_ff_7 (
    .J(or_5_out), .K(or_5_out), .clk(CLK), .Q(out_7[2]), .Qn(j_k_ff_7_qn));  // open: preset, reset
  or or_5 (or_5_out, and_7_out, and_8_out);
  J_K_Flip_Flop j_k_ff_8 (
    .J(or_6_out), .K(or_6_out), .clk(in_4), .Q(out_8[2]), .Qn(j_k_ff_8_qn));  // open: preset, reset
  or or_6 (or_6_out, and_9_out, and_10_out);
  J_K_Flip_Flop j_k_ff_9 (
    .J(or_4_out), .K(or_4_out), .clk(in_6), .Q(out_9[2]), .Qn(j_k_ff_9_qn));  // open: preset, reset
  and and_13 (and_13_out, and_7_out, out_7[2]);
  and and_14 (and_14_out, j_k_ff_7_qn, and_8_out);
  and and_15 (and_15_out, and_9_out, out_8[2]);
  and and_16 (and_16_out, j_k_ff_8_qn, and_10_out);
  and and_17 (and_17_out, and_11_out, out_9[2]);
  and and_18 (and_18_out, j_k_ff_9_qn, and_12_out);
  or or_7 (or_7_out, and_13_out, and_14_out);
  or or_8 (or_8_out, and_15_out, and_16_out);
  J_K_Flip_Flop j_k_ff_10 (.J(or_9_out), .K(or_9_out), .clk(in_6), .Q(out_9[3]));  // open: Qn, preset, reset
  or or_9 (or_9_out, and_17_out, and_18_out);
  J_K_Flip_Flop j_k_ff_11 (.J(or_7_out), .K(or_7_out), .clk(CLK), .Q(out_7[3]));  // open: Qn, preset, reset
  J_K_Flip_Flop j_k_ff_12 (.J(or_8_out), .K(or_8_out), .clk(in_4), .Q(out_8[3]));  // open: Qn, preset, reset
endmodule

module bit3cpr (
  input  [3:0] a1,
  input  [3:0] a2,
  input  [3:0] a3,
  input  [3:0] b1,
  input  [3:0] b2,
  input  [3:0] b3,
  output [1:0] out_7
);

  wire comparator_1_eq, comparator_2_eq, comparator_3_eq;

  Comparator #(.width(4)) comparator_1 (.a(a1), .b(b1), .eq(comparator_1_eq));  // open: gt, lt
  Comparator #(.width(4)) comparator_2 (.a(a2), .b(b2), .eq(comparator_2_eq));  // open: gt, lt
  Comparator #(.width(4)) comparator_3 (.a(a3), .b(b3), .eq(comparator_3_eq));  // open: gt, lt
  Adder #(.width(1)) adder_1 (
    .a(comparator_2_eq), .b(comparator_3_eq), .out(out_7[0]), .cin(comparator_1_eq), .cout(out_7[1]));
endmodule

module ballcounter (
  input  [3:0] a1,
  input  [3:0] a2,
  input  [3:0] a3,
  input  [3:0] b1,
  input  [3:0] b2,
  input  [3:0] b3,
  output [1:0] out_7
);

  wire comparator_1_eq, comparator_2_eq, comparator_3_eq, comparator_4_eq, comparator_5_eq, comparator_6_eq,
       or_1_out, or_2_out, or_3_out;

  Comparator #(.width(4)) comparator_1 (.a(a1), .b(b2), .eq(comparator_1_eq));  // open: gt, lt
  Comparator #(.width(4)) comparator_2 (.a(a1), .b(b3), .eq(comparator_2_eq));  // open: gt, lt
  Comparator #(.width(4)) comparator_3 (.a(a2), .b(b1), .eq(comparator_3_eq));  // open: gt, lt
  or or_1 (or_1_out, comparator_1_eq, comparator_2_eq);
  Comparator #(.width(4)) comparator_4 (.a(a2), .b(b3), .eq(comparator_4_eq));  // open: gt, lt
  Comparator #(.width(4)) comparator_5 (.a(a3), .b(b1), .eq(comparator_5_eq));  // open: gt, lt
  Comparator #(.width(4)) comparator_6 (.a(a3), .b(b2), .eq(comparator_6_eq));  // open: gt, lt
  or or_2 (or_2_out, comparator_3_eq, comparator_4_eq);
  or or_3 (or_3_out, comparator_5_eq, comparator_6_eq);
  Adder #(.width(1)) adder_1 (.a(or_2_out), .b(or_3_out), .out(out_7[0]), .cin(or_1_out), .cout(out_7[1]));
endmodule
